// Logisim project CPUevol_swieta2_rom.circ as structural Verilog: 9 circuits, main circuit ALU1bit
module ALU1bit (
  input  Sub,
  input  Cin,
  input  [2:0] in_3,
  input  A,
  input  B,
  input  Less,
  output Result,
  output Cout,
  output Set
);

  wire and_1_out, not_1_out, or_1_out, or_2_out, xor_1_out;

  xor xor_1 (xor_1_out, Sub, B);
  or or_1 (or_1_out, A, B);
  and and_1 (and_1_out, A, B);
  or or_2 (or_2_out, A, B);
  not not_1 (not_1_out, A);
  Adder #(.width(1)) adder_1 (.a(A), .b(xor_1_out), .out(Set), .cin(Cin), .cout(Cout));
  Multiplexer #(.select(3), .enable("false")) multiplexer_1 (
    .in0(or_1_out), .in1(and_1_out), .in2(or_2_out), .in3(not_1_out), .in4(Set), .in5(Less), .out(Result),
    .sel(in_3));  // open: in6, in7
endmodule

module ALU8bit (
  input  Cin,
  input  Sub,
  input  [2:0] Op,
  input  [7:0] A,
  input  [7:0] B,
  output [7:0] R,
  output Zero,
  output Cout
);

  wire alu1bit_1_cout, alu1bit_2_cout, alu1bit_3_cout, alu1bit_4_cout, alu1bit_5_cout, alu1bit_6_cout,
       alu1bit_7_cout, alu1bit_8_set, or_1_out;

  or or_1 (or_1_out, Sub, Cin);
  ALU1bit alu1bit_1 (
    .A(A[0]), .B(B[0]), .Less(alu1bit_8_set), .Result(R[0]), .Sub(Sub), .Cin(or_1_out), .in_3(Op),
    .Cout(alu1bit_1_cout));  // open: Set
  ALU1bit alu1bit_2 (
    .A(A[1]), .B(B[1]), .Less(1'b0), .Result(R[1]), .Sub(Sub), .Cin(alu1bit_1_cout), .in_3(Op),
    .Cout(alu1bit_2_cout));  // open: Set
  ALU1bit alu1bit_3 (
    .A(A[2]), .B(B[2]), .Less(1'b0), .Result(R[2]), .Sub(Sub), .Cin(alu1bit_2_cout), .in_3(Op),
    .Cout(alu1bit_3_cout));  // open: Set
  ALU1bit alu1bit_4 (
    .A(A[3]), .B(B[3]), .Less(1'b0), .Result(R[3]), .Sub(Sub), .Cin(alu1bit_3_cout), .in_3(Op),
    .Cout(alu1bit_4_cout));  // open: Set
  ALU1bit alu1bit_5 (
    .A(A[4]), .B(B[4]), .Less(1'b0), .Result(R[4]), .Sub(Sub), .Cin(alu1bit_4_cout), .in_3(Op),
    .Cout(alu1bit_5_cout));  // open: Set
  ALU1bit alu1bit_6 (
    .A(A[5]), .B(B[5]), .Less(1'b0), .Result(R[5]), .Sub(Sub), .Cin(alu1bit_5_cout), .in_3(Op),
    .Cout(alu1bit_6_cout));  // open: Set
  ALU1bit alu1bit_7 (
    .A(A[6]), .B(B[6]), .Less(1'b0), .Result(R[6]), .Sub(Sub), .Cin(alu1bit_6_cout), .in_3(Op),
    .Cout(alu1bit_7_cout));  // open: Set
  ALU1bit alu1bit_8 (
    .A(A[7]), .B(B[7]), .Result(R[7]), .Sub(Sub), .Cin(alu1bit_7_cout), .in_3(Op), .Cout(Cout),
    .Set(alu1bit_8_set));  // open: Less
  nor nor_1 (Zero, R[7], R[6], R[5], R[4], R[3], R[2], R[1], R[0]);
endmodule

module CPU (
  input  in_1,
  input  in_2,
  input  in_3,
  input  [7:0] in_4
);

  wire clock_1_out, clock_2_clk_2, clock_2_clke, clock_2_clks, controlsection_1_acc_e,
       controlsection_1_acc_s, controlsection_1_iar_e, controlsection_1_iar_inc, controlsection_1_iar_s,
       controlsection_1_ir_s, controlsection_1_mar_s, controlsection_1_r0_e, controlsection_1_r0_s,
       controlsection_1_r1_e, controlsection_1_r1_s, controlsection_1_r2_e, controlsection_1_r2_s,
       controlsection_1_r3_e, controlsection_1_r3_s, controlsection_1_ram_e, controlsection_1_ram_s,
       controlsection_1_tmp_s, or_1_out;
  wire [2:0] controlsection_1_alu;
  wire [7:0] ACC_q, Address_bufor_q, alu8bit_1_r, controlled_buffer_1_out, IAR_2_q, IR_q, ram_2_dout, reg0_q,
       reg1_q, reg2_q, reg3_q, Temp_q, undriven;

  Register Temp (.D(controlled_buffer_1_out), .clk(controlsection_1_tmp_s), .Q(Temp_q));  // open: en, clr
  ALU8bit alu8bit_1 (
    .A(controlled_buffer_1_out), .B(Temp_q), .R(alu8bit_1_r), .Sub(in_1), .Op(controlsection_1_alu));  // open: Zero, Cout, Cin
  Register ACC (.D(alu8bit_1_r), .clk(controlsection_1_acc_s), .Q(ACC_q));  // open: en, clr
  assign controlled_buffer_1_out = controlsection_1_acc_e ? ACC_q : 8'bz;  // Controlled_Buffer controlled_buffer_1
  Clock_part clock_1 (.out(clock_1_out));
  Flags flags_1 ();  // open: CF, Less, nw, Zero, CF_2, Less_2, nw_2, Zero_2, en
  Clock clock_2 (.clk_2(clock_2_clk_2), .clks(clock_2_clks), .clke(clock_2_clke), .Clk(clock_1_out));
  Register IAR ();  // open: D, en, Q, clk, clr
  Register reg0 (.D(controlled_buffer_1_out), .clk(controlsection_1_r0_s), .Q(reg0_q));  // open: en, clr
  Counter IAR_2 (
    .clr(in_2), .load(controlsection_1_iar_s), .clk(controlsection_1_iar_inc), .D(controlled_buffer_1_out),
    .Q(IAR_2_q));  // open: up, count, carry
  Register reg1 (.D(controlled_buffer_1_out), .clk(controlsection_1_r1_s), .Q(reg1_q));  // open: en, clr
  assign controlled_buffer_1_out = controlsection_1_r0_e ? reg0_q : 8'bz;  // Controlled_Buffer controlled_buffer_2
  assign controlled_buffer_1_out = controlsection_1_r1_e ? reg1_q : 8'bz;  // Controlled_Buffer controlled_buffer_3
  assign controlled_buffer_1_out = controlsection_1_iar_e ? IAR_2_q : 8'bz;  // Controlled_Buffer controlled_buffer_4
  Register reg2 (.D(controlled_buffer_1_out), .clk(controlsection_1_r2_s), .Q(reg2_q));  // open: en, clr
  Register IR (.D(controlled_buffer_1_out), .clk(controlsection_1_ir_s), .Q(IR_q));  // open: en, clr
  Register reg3 (.D(controlled_buffer_1_out), .clk(controlsection_1_r3_s), .Q(reg3_q));  // open: en, clr
  assign controlled_buffer_1_out = controlsection_1_r2_e ? reg2_q : 8'bz;  // Controlled_Buffer controlled_buffer_5
  assign controlled_buffer_1_out = controlsection_1_r3_e ? reg3_q : 8'bz;  // Controlled_Buffer controlled_buffer_6
  RAM #(.databus("bibus")) ram_1 (.addr(undriven), .we(in_3), .clk(in_3), .din(in_4));  // open: oe, dout
  ControlSection controlsection_1 (
    .clks(clock_2_clks), .clk(clock_2_clk_2), .clke(clock_2_clke), .RAM_E(controlsection_1_ram_e),
    .ACC_E(controlsection_1_acc_e), .R0_E(controlsection_1_r0_e), .R1_E(controlsection_1_r1_e),
    .R2_E(controlsection_1_r2_e), .R3_E(controlsection_1_r3_e), .ALU(controlsection_1_alu),
    .MAR_S(controlsection_1_mar_s), .ACC_S(controlsection_1_acc_s), .RAM_S(controlsection_1_ram_s),
    .TMP_S(controlsection_1_tmp_s), .R0_S(controlsection_1_r0_s), .R1_S(controlsection_1_r1_s),
    .R2_S(controlsection_1_r2_s), .R3_S(controlsection_1_r3_s), .IR_input(IR_q),
    .IAR_E(controlsection_1_iar_e), .IR_S(controlsection_1_ir_s), .IAR_S(controlsection_1_iar_s),
    .IAR_INC(controlsection_1_iar_inc));
  or or_1 (or_1_out, controlsection_1_mar_s, controlsection_1_ram_s);
  Register Address_bufor (
    .D(controlled_buffer_1_out), .clk(controlsection_1_mar_s), .Q(Address_bufor_q));  // open: en, clr
  RAM #(.databus("bibus")) ram_2 (
    .addr(Address_bufor_q), .we(controlsection_1_ram_s), .oe(controlsection_1_ram_e), .clk(or_1_out),
    .din(controlled_buffer_1_out), .dout(ram_2_dout));
  assign controlled_buffer_1_out = controlsection_1_ram_e ? ram_2_dout : 8'bz;  // Controlled_Buffer controlled_buffer_7
endmodule

module Clock (
  input  Clk,
  output clk_2,
  output clks,
  output clke
);

  wire j_k_ff_1_qn, nand_1_out;

  J_K_Flip_Flop j_k_ff_1 (.J(1'b1), .K(1'b1), .clk(Clk), .Q(clk_2), .Qn(j_k_ff_1_qn));  // open: preset, reset
  nand nand_1 (nand_1_out, Clk, clk_2);
  nand nand_2 (clke, j_k_ff_1_qn, Clk);
  not not_1 (clks, nand_1_out);
endmodule

module ControlSection (
  input  clks,
  input  clk,
  input  clke,
  input  [7:0] IR_input,
  output MAR_S,
  output RAM_E,
  output ACC_S,
  output RAM_S,
  output TMP_S,
  output ACC_E,
  output IAR_E,
  output IR_S,
  output IAR_S,
  output IAR_INC,
  output R0_S,
  output R1_S,
  output R2_S,
  output R3_S,
  output R0_E,
  output R1_E,
  output R2_E,
  output R3_E,
  output [2:0] ALU
);

  wire ACC_E_t, ACC_S_t, and_4_out, and_5_out, and_6_out, and_7_out, and_8_out, and_9_out, and_10_out,
       and_11_out, DATA, decoder_1_out0, decoder_1_out1, decoder_1_out2, decoder_1_out3, decoder_2_out0,
       decoder_2_out1, decoder_2_out2, decoder_2_out3, decoder_3_out0, decoder_4_out0, decoder_6_out0,
       decoder_6_out1, decoder_6_out2, decoder_6_out3, IAR_E_t, IAR_S_t, IR_S_t, LOAD, MAR_S_t, not_1_out,
       RAM_E_t, RAM_S_t, REGA_E, REGB_E, REGB_S, STEP_1, STEP_2, STEP_3, STEP_4, STEP_5, STEP_6, STORE,
       TMP_S_t, xnor_1_out;
  wire [2:0] controlled_buffer_13_out;
  wire [3:0] controlled_buffer_1_out, controlled_buffer_2_out;
  wire [7:0] controlled_buffer_6_out, rom_1_data;

  and and_1 (RAM_E, clke, RAM_E_t);
  and and_2 (ACC_E, clke, ACC_E_t);
  and and_3 (IAR_E, clke, IAR_E_t);
  or or_1 (R0_E, and_4_out, and_8_out);
  or or_2 (R1_E, and_5_out, and_9_out);
  or or_3 (R2_E, and_6_out, and_10_out);
  or or_4 (R3_E, and_7_out, and_11_out);
  and and_4 (and_4_out, REGB_E, clke, decoder_1_out0);
  and and_5 (and_5_out, REGB_E, clke, decoder_1_out1);
  and and_6 (and_6_out, REGB_E, clke, decoder_1_out2);
  and and_7 (and_7_out, REGB_E, clke, decoder_1_out3);
  and and_8 (and_8_out, REGA_E, clke, decoder_2_out0);
  and and_9 (and_9_out, REGA_E, clke, decoder_2_out1);
  and and_10 (and_10_out, REGA_E, clke, decoder_2_out2);
  and and_11 (and_11_out, REGA_E, clke, decoder_2_out3);
  assign controlled_buffer_1_out = STEP_6 ? 4'b0011 : 4'bz;  // Controlled_Buffer controlled_buffer_1
  assign controlled_buffer_2_out = IR_input[7] ? 4'b0000 : 4'bz;  // Controlled_Buffer controlled_buffer_2
  assign controlled_buffer_2_out = LOAD ? 4'b0001 : 4'bz;  // Controlled_Buffer controlled_buffer_3
  assign controlled_buffer_2_out = STORE ? 4'b0010 : 4'bz;  // Controlled_Buffer controlled_buffer_4
  assign controlled_buffer_2_out = DATA ? 4'b0011 : 4'bz;  // Controlled_Buffer controlled_buffer_5
  StepperV2 stepperv2_1 (
    .CLOCK(clk), .step_3(STEP_3), .step_4(STEP_4), .step_6(STEP_6), .step_1(STEP_1), .step_2(STEP_2),
    .step_5(STEP_5));  // open: reset, step_7
  assign controlled_buffer_6_out = STEP_1 ? {8{1'b0}} : 8'bz;  // Controlled_Buffer controlled_buffer_6
  assign controlled_buffer_1_out = STEP_4 ? 4'b0001 : 4'bz;  // Controlled_Buffer controlled_buffer_7
  assign controlled_buffer_1_out = STEP_5 ? 4'b0010 : 4'bz;  // Controlled_Buffer controlled_buffer_8
  Decoder #(.select(2)) decoder_1 (
    .out0(decoder_1_out0), .out1(decoder_1_out1), .out2(decoder_1_out2), .out3(decoder_1_out3),
    .sel(IR_input[1:0]));  // open: en
  Decoder #(.select(2)) decoder_2 (
    .out0(decoder_2_out0), .out1(decoder_2_out1), .out2(decoder_2_out2), .out3(decoder_2_out3),
    .sel(IR_input[3:2]));  // open: en
  assign ALU = STEP_5 ? controlled_buffer_13_out : 3'bz;  // Controlled_Buffer controlled_buffer_9
  assign controlled_buffer_6_out = STEP_2 ? 8'h1 : 8'bz;  // Controlled_Buffer controlled_buffer_10
  assign controlled_buffer_6_out = STEP_3 ? 8'h2 : 8'bz;  // Controlled_Buffer controlled_buffer_11
  assign controlled_buffer_6_out = xnor_1_out ? {controlled_buffer_1_out, controlled_buffer_2_out} : 8'bz;  // Controlled_Buffer controlled_buffer_12
  NotExactlyOne xnor_1 (.out(xnor_1_out), .in0(STEP_1), .in1(STEP_2), .in2(STEP_3));
  Decoder #(.select(4)) decoder_3 (
    .out0(decoder_3_out0), .out1(RAM_E_t), .out2(IAR_E_t), .out3(REGA_E), .out4(REGB_E), .out5(ACC_E_t),
    .sel(rom_1_data[7:4]));  // open: out6, out7, out8, out9, out10, out11, out12, out13, out14, out15, en
  ROM rom_1 (.addr(controlled_buffer_6_out), .data(rom_1_data));
  assign controlled_buffer_13_out = IR_input[7] ? IR_input[6:4] : 3'bz;  // Controlled_Buffer controlled_buffer_13
  Decoder #(.select(4)) decoder_4 (
    .out0(decoder_4_out0), .out1(IR_S_t), .out2(MAR_S_t), .out3(ACC_S_t), .out4(TMP_S_t), .out5(REGB_S),
    .out6(IAR_S_t), .out7(RAM_S_t), .out8(IAR_INC), .sel(rom_1_data[3:0]));  // open: out9, out10, out11, out12, out13, out14, out15, en
  not not_1 (not_1_out, IR_input[7]);
  Decoder #(.select(3)) decoder_5 (
    .out0(LOAD), .out1(STORE), .out2(DATA), .sel(IR_input[6:4]), .en(not_1_out));  // open: out3, out4, out5, out6, out7
  Decoder #(.select(2)) decoder_6 (
    .out0(decoder_6_out0), .out1(decoder_6_out1), .out2(decoder_6_out2), .out3(decoder_6_out3),
    .sel(IR_input[1:0]));  // open: en
  and and_12 (MAR_S, clks, MAR_S_t);
  and and_13 (ACC_S, clks, ACC_S_t);
  and and_14 (RAM_S, clks, RAM_S_t);
  and and_15 (TMP_S, clks, TMP_S_t);
  and and_16 (IR_S, clks, IR_S_t);
  and and_17 (IAR_S, clks, IAR_S_t);
  and and_18 (R0_S, clks, REGB_S, decoder_6_out0);
  and and_19 (R1_S, clks, REGB_S, decoder_6_out1);
  and and_20 (R2_S, clks, REGB_S, decoder_6_out2);
  and and_21 (R3_S, clks, REGB_S, decoder_6_out3);

  // Other names for the same wires on the sheet: ALU_INS = IR_input[7]

  // Notes on the sheet:
  //   REG B
  //   REG A
  //   contents of rom_1 (hex, n*v repeats v):
  //   22 11 8 13*0 44 15*0 33 15*0 55
  //   REG B
endmodule

module Mem1bit (
  input  set,
  input  enable,
  output out_3
);

  wire nand_1_out, nand_2_out, nand_4_out;

  nand nand_1 (nand_1_out, set, enable);
  nand nand_2 (nand_2_out, nand_1_out, enable);
  nand nand_3 (out_3, nand_1_out, nand_4_out);
  nand nand_4 (nand_4_out, out_3, nand_2_out);
endmodule

module Flags (
  input  CF,
  input  Less,
  input  nw,
  input  Zero,
  input  en,
  output CF_2,
  output Less_2,
  output nw_2,
  output Zero_2
);

  // Mem1bit mem1bit_1: pin names not known; wires that end beside it: CF, en, Less, CF_2
  // Mem1bit mem1bit_2: pin names not known; wires that end beside it: Less, en, nw, Less_2
  // Mem1bit mem1bit_3: pin names not known; wires that end beside it: nw, en, Zero, nw_2
  // Mem1bit mem1bit_4: pin names not known; wires that end beside it: Zero, en, Zero_2
endmodule

module Stepper (
  input  reset,
  input  clk,
  output step1,
  output step2,
  output step3,
  output step4,
  output step5,
  output step6,
  output step7
);

  wire mem1bit_1_out_3, mem1bit_2_out_3, mem1bit_3_out_3, mem1bit_4_out_3, mem1bit_5_out_3, mem1bit_6_out_3,
       mem1bit_7_out_3, mem1bit_8_out_3, mem1bit_9_out_3, mem1bit_10_out_3, mem1bit_11_out_3, not_1_out,
       not_2_out, not_3_out, not_4_out, not_5_out, not_6_out, not_7_out, not_8_out, or_1_out, or_2_out;

  or or_1 (or_1_out, reset, clk);
  or or_2 (or_2_out, reset, not_1_out);
  not not_1 (not_1_out, clk);
  or or_3 (step1, reset, not_3_out);
  not not_2 (not_2_out, reset);
  not not_3 (not_3_out, mem1bit_2_out_3);
  Mem1bit mem1bit_1 (.set(not_2_out), .enable(or_1_out), .out_3(mem1bit_1_out_3));
  Mem1bit mem1bit_2 (.set(mem1bit_1_out_3), .enable(or_2_out), .out_3(mem1bit_2_out_3));
  and and_1 (step2, mem1bit_2_out_3, not_4_out);
  not not_4 (not_4_out, mem1bit_4_out_3);
  Mem1bit mem1bit_3 (.set(mem1bit_2_out_3), .enable(or_1_out), .out_3(mem1bit_3_out_3));
  Mem1bit mem1bit_4 (.set(mem1bit_3_out_3), .enable(or_2_out), .out_3(mem1bit_4_out_3));
  and and_2 (step3, mem1bit_4_out_3, not_5_out);
  not not_5 (not_5_out, mem1bit_6_out_3);
  Mem1bit mem1bit_5 (.set(mem1bit_4_out_3), .enable(or_1_out), .out_3(mem1bit_5_out_3));
  Mem1bit mem1bit_6 (.set(mem1bit_5_out_3), .enable(or_2_out), .out_3(mem1bit_6_out_3));
  and and_3 (step4, mem1bit_6_out_3, not_6_out);
  Mem1bit mem1bit_7 (.set(mem1bit_6_out_3), .enable(or_1_out), .out_3(mem1bit_7_out_3));
  not not_6 (not_6_out, mem1bit_8_out_3);
  Mem1bit mem1bit_8 (.set(mem1bit_7_out_3), .enable(or_2_out), .out_3(mem1bit_8_out_3));
  and and_4 (step5, mem1bit_8_out_3, not_7_out);
  not not_7 (not_7_out, mem1bit_10_out_3);
  Mem1bit mem1bit_9 (.set(mem1bit_8_out_3), .enable(or_1_out), .out_3(mem1bit_9_out_3));
  Mem1bit mem1bit_10 (.set(mem1bit_9_out_3), .enable(or_2_out), .out_3(mem1bit_10_out_3));
  and and_5 (step6, mem1bit_10_out_3, not_8_out);
  not not_8 (not_8_out, step7);
  Mem1bit mem1bit_11 (.set(mem1bit_10_out_3), .enable(or_1_out), .out_3(mem1bit_11_out_3));
  Mem1bit mem1bit_12 (.set(mem1bit_11_out_3), .enable(or_2_out), .out_3(step7));
endmodule

module StepperV2 (
  input  reset,
  input  CLOCK,
  output step_3,
  output step_4,
  output step_6,
  output step_7,
  output step_1,
  output step_2,
  output step_5
);

  wire d_ff_1_q, d_ff_2_q, d_ff_3_q, d_ff_4_q, d_ff_5_q, d_ff_6_q, d_ff_7_q, d_ff_8_q, d_ff_9_q, d_ff_10_q,
       d_ff_11_q, d_ff_12_q, d_ff_13_q, d_ff_14_q, not_1_out, not_2_out, not_4_out, not_5_out, not_6_out,
       not_7_out, not_8_out, not_9_out, or_1_out, or_2_out, or_3_out;

  not not_1 (not_1_out, CLOCK);
  not not_2 (not_2_out, reset);
  or or_1 (or_1_out, 1'b0, CLOCK);
  or or_2 (or_2_out, 1'b0, not_1_out);
  D_Flip_Flop d_ff_1 (.D(not_2_out), .clk(or_1_out), .Q(d_ff_1_q), .reset(or_3_out));  // open: Qn, preset
  not not_3 (step_1, d_ff_2_q);
  D_Flip_Flop d_ff_2 (.D(d_ff_1_q), .clk(or_2_out), .Q(d_ff_2_q), .reset(or_3_out));  // open: Qn, preset
  and and_1 (step_2, d_ff_2_q, not_4_out);
  D_Flip_Flop d_ff_3 (.D(d_ff_2_q), .clk(or_1_out), .Q(d_ff_3_q), .reset(or_3_out));  // open: Qn, preset
  D_Flip_Flop d_ff_4 (.D(d_ff_3_q), .clk(or_2_out), .Q(d_ff_4_q), .reset(or_3_out));  // open: Qn, preset
  not not_4 (not_4_out, d_ff_4_q);
  D_Flip_Flop d_ff_5 (.D(d_ff_4_q), .clk(or_1_out), .Q(d_ff_5_q), .reset(or_3_out));  // open: Qn, preset
  and and_2 (step_3, d_ff_4_q, not_5_out);
  not not_5 (not_5_out, d_ff_6_q);
  D_Flip_Flop d_ff_6 (.D(d_ff_5_q), .clk(or_2_out), .Q(d_ff_6_q), .reset(or_3_out));  // open: Qn, preset
  and and_3 (step_4, d_ff_6_q, not_6_out);
  D_Flip_Flop d_ff_7 (.D(d_ff_6_q), .clk(or_1_out), .Q(d_ff_7_q), .reset(or_3_out));  // open: Qn, preset
  not not_6 (not_6_out, d_ff_8_q);
  D_Flip_Flop d_ff_8 (.D(d_ff_7_q), .clk(or_2_out), .Q(d_ff_8_q), .reset(or_3_out));  // open: Qn, preset
  and and_4 (step_5, d_ff_8_q, not_7_out);
  D_Flip_Flop d_ff_9 (.D(d_ff_8_q), .clk(or_1_out), .Q(d_ff_9_q), .reset(or_3_out));  // open: Qn, preset
  not not_7 (not_7_out, d_ff_10_q);
  D_Flip_Flop d_ff_10 (.D(d_ff_9_q), .clk(or_2_out), .Q(d_ff_10_q), .reset(or_3_out));  // open: Qn, preset
  and and_5 (step_6, d_ff_10_q, not_8_out);
  D_Flip_Flop d_ff_11 (.D(d_ff_10_q), .clk(or_1_out), .Q(d_ff_11_q), .reset(or_3_out));  // open: Qn, preset
  not not_8 (not_8_out, d_ff_12_q);
  D_Flip_Flop d_ff_12 (.D(d_ff_11_q), .clk(or_2_out), .Q(d_ff_12_q), .reset(or_3_out));  // open: Qn, preset
  and and_6 (step_7, d_ff_12_q, not_9_out);
  D_Flip_Flop d_ff_13 (.D(d_ff_12_q), .clk(or_1_out), .Q(d_ff_13_q), .reset(or_3_out));  // open: Qn, preset
  not not_9 (not_9_out, d_ff_14_q);
  D_Flip_Flop d_ff_14 (.D(d_ff_13_q), .clk(or_2_out), .Q(d_ff_14_q), .reset(or_3_out));  // open: Qn, preset
  or or_3 (or_3_out, reset, d_ff_14_q);
endmodule
