// Logisim project alu3_5.circ as structural Verilog: 8 circuits, main circuit main
module main (
  input  CIN_IM,
  input  CIN_RE,
  input  [7:0] A,
  input  [7:0] B,
  input  [7:0] C,
  input  [7:0] D,
  input  [2:0] OPERATION,
  output [7:0] RESULT_A,
  output [7:0] RESULT_B,
  output COUT_RE,
  output COUT_IM,
  output DIV_BY_0
);

  wire adder_re_im_1_cout_im, adder_re_im_1_cout_re, div_re_im_1_div_0_error, div_re_im_1_imag_ov,
       div_re_im_1_real_ov, mult_re_im_1_imag_ov, mult_re_im_1_real_ov, sub_re_im_1_cout_im,
       sub_re_im_1_cout_re;
  wire [7:0] adder_re_im_1_result_im, adder_re_im_1_result_real, div_re_im_1_result_im,
       div_re_im_1_result_real, mult_re_im_1_result_im, mult_re_im_1_result_real, sub_re_im_1_result_im,
       sub_re_im_1_result_real;

  ADDER_RE_IM adder_re_im_1 (
    .RESULT_REAL(adder_re_im_1_result_real), .COUT_RE(adder_re_im_1_cout_re),
    .RESULT_IM(adder_re_im_1_result_im), .COUT_IM(adder_re_im_1_cout_im), .A(A), .B(B), .C(C), .D(D),
    .CIN_RE(CIN_RE), .CIN_IM(CIN_IM));
  SUB_RE_IM sub_re_im_1 (
    .RESULT_REAL(sub_re_im_1_result_real), .COUT_RE(sub_re_im_1_cout_re), .RESULT_IM(sub_re_im_1_result_im),
    .COUT_IM(sub_re_im_1_cout_im), .A(A), .B(B), .C(C), .D(D), .CIN_RE(CIN_RE), .CIN_IM(CIN_IM));
  MULT_RE_IM mult_re_im_1 (
    .RESULT_REAL(mult_re_im_1_result_real), .REAL_OV(mult_re_im_1_real_ov),
    .RESULT_IM(mult_re_im_1_result_im), .IMAG_OV(mult_re_im_1_imag_ov), .A(A), .B(B), .C(C), .D(D));
  DIV_RE_IM div_re_im_1 (
    .RESULT_REAL(div_re_im_1_result_real), .REAL_OV(div_re_im_1_real_ov),
    .DIV_0_error(div_re_im_1_div_0_error), .RESULT_IM(div_re_im_1_result_im), .IMAG_OV(div_re_im_1_imag_ov),
    .A(A), .B(B), .C(C), .D(D));
  Multiplexer #(.select(3), .width(8), .enable("false")) multiplexer_1 (
    .in1(adder_re_im_1_result_real), .in2(sub_re_im_1_result_real), .in3(mult_re_im_1_result_real),
    .in4(div_re_im_1_result_real), .out(RESULT_A), .sel(OPERATION));  // open: in0, in5, in6, in7
  Multiplexer #(.select(3), .width(8), .enable("false")) multiplexer_2 (
    .in1(adder_re_im_1_result_im), .in2(sub_re_im_1_result_im), .in3(mult_re_im_1_result_im),
    .in4(div_re_im_1_result_im), .out(RESULT_B), .sel(OPERATION));  // open: in0, in5, in6, in7
  Multiplexer #(.select(3), .enable("false")) multiplexer_3 (
    .in1(adder_re_im_1_cout_re), .in2(sub_re_im_1_cout_re), .in3(mult_re_im_1_real_ov),
    .in4(div_re_im_1_real_ov), .out(COUT_RE), .sel(OPERATION));  // open: in0, in5, in6, in7
  Multiplexer #(.select(3), .enable("false")) multiplexer_4 (
    .in1(adder_re_im_1_cout_im), .in2(sub_re_im_1_cout_im), .in3(mult_re_im_1_imag_ov),
    .in4(div_re_im_1_imag_ov), .out(COUT_IM), .sel(OPERATION));  // open: in0, in5, in6, in7
  Multiplexer #(.select(3), .enable("false")) multiplexer_5 (
    .in0(1'b0), .in1(1'b0), .in2(1'b0), .in3(1'b0), .in4(div_re_im_1_div_0_error), .in5(1'b0), .in6(1'b0),
    .in7(1'b0), .out(DIV_BY_0), .sel(OPERATION));

  // Other names for the same wires on the sheet: cin_im_t = CIN_IM; cin_re_t = CIN_RE; im1_t[7:0] = B; im2_t[7:0] = D;
  //   re1_t[7:0] = A; re2_t[7:0] = C

  // Notes on the sheet:
  //   pierwsza liczba
  //   A-re, B-im
  //   C-re, D-im
  //   druga liczba
  //   wybór operacji
  //   001- dodawanie
  //   010 - odejmowanie
  //   011- mnozenie
  //   100- dzielenie
endmodule

module ADDER8bit (
  input  CIN,
  input  [7:0] ARG1,
  input  [7:0] ARG2,
  output [7:0] RESULT,
  output COUT
);

  Adder adder_1 (.a(ARG1), .b(ARG2), .out(RESULT), .cin(CIN), .cout(COUT));
endmodule

module ADDER_RE_IM (
  input  [7:0] A,
  input  [7:0] B,
  input  [7:0] C,
  input  [7:0] D,
  input  CIN_RE,
  input  CIN_IM,
  output [7:0] RESULT_REAL,
  output COUT_RE,
  output [7:0] RESULT_IM,
  output COUT_IM
);

  ADDER8bit adder8bit_1 (.ARG1(A), .ARG2(C), .RESULT(RESULT_REAL), .COUT(COUT_RE), .CIN(CIN_RE));
  ADDER8bit adder8bit_2 (.ARG1(B), .ARG2(D), .RESULT(RESULT_IM), .COUT(COUT_IM), .CIN(CIN_IM));
endmodule

module SUB8bit (
  input  CIN,
  input  [7:0] ARG1,
  input  [7:0] ARG2,
  output [7:0] RESULT,
  output COUT
);

  Subtractor subtractor_1 (.a(ARG1), .b(ARG2), .out(RESULT), .bin(CIN), .bout(COUT));
endmodule

module SUB_RE_IM (
  input  [7:0] A,
  input  [7:0] B,
  input  [7:0] C,
  input  [7:0] D,
  input  CIN_RE,
  input  CIN_IM,
  output [7:0] RESULT_REAL,
  output COUT_RE,
  output [7:0] RESULT_IM,
  output COUT_IM
);

  SUB8bit sub8bit_1 (.ARG1(A), .ARG2(C), .RESULT(RESULT_REAL), .COUT(COUT_RE), .CIN(CIN_RE));
  SUB8bit sub8bit_2 (.ARG1(B), .ARG2(D), .RESULT(RESULT_IM), .COUT(COUT_IM), .CIN(CIN_IM));
endmodule

module MULT_RE_IM (
  input  [7:0] A,
  input  [7:0] B,
  input  [7:0] C,
  input  [7:0] D,
  output [7:0] RESULT_REAL,
  output REAL_OV,
  output [7:0] RESULT_IM,
  output IMAG_OV
);

  wire adder_1_cout, adder_2_cout, subtractor_1_bout;
  wire [7:0] adder_2_out, multiplier_1_cout, multiplier_1_out, multiplier_2_cout, multiplier_2_out,
       multiplier_3_cout, multiplier_3_out, multiplier_4_cout, multiplier_4_out, subtractor_2_out;

  Multiplier multiplier_1 (.a(A), .b(C), .out(multiplier_1_out), .cout(multiplier_1_cout));  // open: cin
  Multiplier multiplier_2 (.a(B), .b(D), .out(multiplier_2_out), .cout(multiplier_2_cout));  // open: cin
  Multiplier multiplier_3 (.a(B), .b(C), .out(multiplier_3_out), .cout(multiplier_3_cout));  // open: cin
  Multiplier multiplier_4 (.a(A), .b(D), .out(multiplier_4_out), .cout(multiplier_4_cout));  // open: cin
  Subtractor subtractor_1 (
    .a(multiplier_1_out), .b(multiplier_2_out), .out(RESULT_REAL), .bout(subtractor_1_bout));  // open: bin
  Subtractor subtractor_2 (
    .a(multiplier_1_cout), .b(multiplier_2_cout), .out(subtractor_2_out), .bin(subtractor_1_bout));  // open: bout
  Adder adder_1 (.a(multiplier_3_out), .b(multiplier_4_out), .out(RESULT_IM), .cout(adder_1_cout));  // open: cin
  Adder adder_2 (
    .a(multiplier_3_cout), .b(multiplier_4_cout), .out(adder_2_out), .cin(adder_1_cout), .cout(adder_2_cout));
  or or_1 (REAL_OV, subtractor_2_out[0], subtractor_2_out[1], subtractor_2_out[2], subtractor_2_out[3], subtractor_2_out[4], subtractor_2_out[5], subtractor_2_out[6], subtractor_2_out[7]);
  or or_2 (IMAG_OV, adder_2_out[0], adder_2_out[1], adder_2_out[2], adder_2_out[3], adder_2_out[4], adder_2_out[5], adder_2_out[6], adder_2_out[7], adder_2_cout);

  // Other names for the same wires on the sheet: A_t[7:0] = A; B_t[7:0] = B; C_t[7:0] = C; D_t[7:0] = D

  // Notes on the sheet:
  //   wszystko wedle wzoru : (ac-bd)+(bc+ad)i
  //   (ac)
  //   (bd)
  //   bc
  //   ad
  //   (starsze bity)
  //   (starsze bity)
  //   (starsze bity)
  //   (starsze bity)
  //   (ac-bd)
endmodule

module DIV_RE_IM (
  input  [7:0] A,
  input  [7:0] B,
  input  [7:0] C,
  input  [7:0] D,
  output [7:0] RESULT_REAL,
  output REAL_OV,
  output DIV_0_error,
  output [7:0] RESULT_IM,
  output IMAG_OV
);

  wire adder_1_cout, adder_3_cout, subtractor_1_bout;
  wire [7:0] adder_1_out, adder_2_out, adder_3_out, adder_4_out, multiplier_1_cout, multiplier_1_out,
       multiplier_2_cout, multiplier_2_out, multiplier_3_cout, multiplier_3_out, multiplier_4_cout,
       multiplier_4_out, multiplier_5_cout, multiplier_5_out, multiplier_6_cout, multiplier_6_out,
       subtractor_1_out, subtractor_2_out;
  wire [16:0] divider_1_rem, divider_2_rem;
  wire [16:8] divider_1_out, divider_2_out;
  wire [16:16] adder_2_cout, adder_4_cout, subtractor_2_bout;

  Multiplier multiplier_1 (.a(A), .b(C), .out(multiplier_1_out), .cout(multiplier_1_cout));  // open: cin
  Multiplier multiplier_2 (.a(B), .b(D), .out(multiplier_2_out), .cout(multiplier_2_cout));  // open: cin
  Multiplier multiplier_3 (.a(C), .b(C), .out(multiplier_3_out), .cout(multiplier_3_cout));  // open: cin
  Multiplier multiplier_4 (.a(D), .b(D), .out(multiplier_4_out), .cout(multiplier_4_cout));  // open: cin
  Multiplier multiplier_5 (.a(B), .b(C), .out(multiplier_5_out), .cout(multiplier_5_cout));  // open: cin
  Multiplier multiplier_6 (.a(A), .b(D), .out(multiplier_6_out), .cout(multiplier_6_cout));  // open: cin
  Adder adder_1 (.a(multiplier_1_out), .b(multiplier_2_out), .out(adder_1_out), .cout(adder_1_cout));  // open: cin
  Adder adder_2 (
    .a(multiplier_1_cout), .b(multiplier_2_cout), .out(adder_2_out), .cin(adder_1_cout),
    .cout(adder_2_cout[16]));
  Adder adder_3 (.a(multiplier_3_out), .b(multiplier_4_out), .out(adder_3_out), .cout(adder_3_cout));  // open: cin
  Adder adder_4 (
    .a(multiplier_3_cout), .b(multiplier_4_cout), .out(adder_4_out), .cin(adder_3_cout),
    .cout(adder_4_cout[16]));
  Subtractor subtractor_1 (
    .a(multiplier_5_out), .b(multiplier_6_out), .out(subtractor_1_out), .bout(subtractor_1_bout));  // open: bin
  Subtractor subtractor_2 (
    .a(multiplier_5_cout), .b(multiplier_6_cout), .out(subtractor_2_out), .bin(subtractor_1_bout),
    .bout(subtractor_2_bout[16]));
  Divider #(.width(17)) divider_1 (
    .a({subtractor_2_bout[16], subtractor_2_out, subtractor_1_out}),
    .b({adder_4_cout[16], adder_4_out, adder_3_out}), .out({divider_1_out, RESULT_IM}), .rem(divider_1_rem));  // open: upper
  Divider #(.width(17)) divider_2 (
    .a({adder_2_cout[16], adder_2_out, adder_1_out}), .b({adder_4_cout[16], adder_4_out, adder_3_out}),
    .out({divider_2_out, RESULT_REAL}), .rem(divider_2_rem));  // open: upper
  nor nor_1 (DIV_0_error, adder_3_out[0], adder_3_out[1], adder_3_out[2], adder_3_out[3], adder_3_out[4], adder_3_out[5], adder_3_out[6], adder_3_out[7], adder_4_out[0], adder_4_out[1], adder_4_out[2], adder_4_out[3], adder_4_out[4], adder_4_out[5], adder_4_out[6], adder_4_out[7], adder_4_cout[16]);
  or or_1 (IMAG_OV, divider_1_out[16], divider_1_out[8], divider_1_out[9], divider_1_out[10], divider_1_out[11], divider_1_out[12], divider_1_out[13], divider_1_out[14], divider_1_out[15]);
  or or_2 (REAL_OV, divider_2_out[16], divider_2_out[8], divider_2_out[9], divider_2_out[10], divider_2_out[11], divider_2_out[12], divider_2_out[13], divider_2_out[14], divider_2_out[15]);

  // Other names for the same wires on the sheet: A_t[7:0] = A; B_t[7:0] = B; C_t[7:0] = C; D_t[7:0] = D

  // Notes on the sheet:
  //   (ac)
  //   (bd)
  //   wedle wzoru (ac+bd)/(c^2 +d^2)
  //   (ac)
  //   (starsze bity)
  //   (bd)
  //   (starsze bity)
  //   (bd)
  //   (starsze bity)
  //   (starsze bity)
  //   (starsze bity)
  //   (starsze bity)
  //   komentarz: co zrobic z resztami? czy 15 bitow to dobre rozwiazanie?
  //   (bc-ad)
  //   (bc-ad)/(c^2+d^2)
  //   (ac+bd)
  //   (c^2+d^2)
  //   reszta
  //   reszta
  //   result_real_high_bits
  //   result_im_high_bits
endmodule

module ALU_v2 (
  input  CIN_RE,
  input  CIN_IM,
  input  [7:0] A,
  input  [7:0] B,
  input  [7:0] C,
  input  [7:0] D,
  input  [2:0] OPERATION,
  output [7:0] RESULT_A,
  output [7:0] RESULT_B,
  output COUT_RE,
  output COUT_IM,
  output DIV_BY_0
);

  wire adder_re_im_1_cout_im, adder_re_im_1_cout_re, div_re_im_1_div_0_error, div_re_im_1_imag_ov,
       div_re_im_1_real_ov, mult_re_im_1_imag_ov, mult_re_im_1_real_ov, sub_re_im_1_cout_im,
       sub_re_im_1_cout_re;
  wire [7:0] adder_re_im_1_result_im, adder_re_im_1_result_real, div_re_im_1_result_im,
       div_re_im_1_result_real, mult_re_im_1_result_im, mult_re_im_1_result_real, sub_re_im_1_result_im,
       sub_re_im_1_result_real;

  ADDER_RE_IM adder_re_im_1 (
    .RESULT_REAL(adder_re_im_1_result_real), .COUT_RE(adder_re_im_1_cout_re),
    .RESULT_IM(adder_re_im_1_result_im), .COUT_IM(adder_re_im_1_cout_im), .A(A), .B(B), .C(C), .D(D),
    .CIN_RE(CIN_RE), .CIN_IM(CIN_IM));
  SUB_RE_IM sub_re_im_1 (
    .RESULT_REAL(sub_re_im_1_result_real), .COUT_RE(sub_re_im_1_cout_re), .RESULT_IM(sub_re_im_1_result_im),
    .COUT_IM(sub_re_im_1_cout_im), .A(A), .B(B), .C(C), .D(D), .CIN_RE(CIN_RE), .CIN_IM(CIN_IM));
  MULT_RE_IM mult_re_im_1 (
    .RESULT_REAL(mult_re_im_1_result_real), .REAL_OV(mult_re_im_1_real_ov),
    .RESULT_IM(mult_re_im_1_result_im), .IMAG_OV(mult_re_im_1_imag_ov), .A(A), .B(B), .C(C), .D(D));
  DIV_RE_IM div_re_im_1 (
    .RESULT_REAL(div_re_im_1_result_real), .REAL_OV(div_re_im_1_real_ov),
    .DIV_0_error(div_re_im_1_div_0_error), .RESULT_IM(div_re_im_1_result_im), .IMAG_OV(div_re_im_1_imag_ov),
    .A(A), .B(B), .C(C), .D(D));
  Multiplexer #(.select(3), .width(8), .enable("false")) multiplexer_1 (
    .in1(adder_re_im_1_result_real), .in2(sub_re_im_1_result_real), .in3(mult_re_im_1_result_real),
    .in4(div_re_im_1_result_real), .out(RESULT_A), .sel(OPERATION));  // open: in0, in5, in6, in7
  Multiplexer #(.select(3), .width(8), .enable("false")) multiplexer_2 (
    .in1(adder_re_im_1_result_im), .in2(sub_re_im_1_result_im), .in3(mult_re_im_1_result_im),
    .in4(div_re_im_1_result_im), .out(RESULT_B), .sel(OPERATION));  // open: in0, in5, in6, in7
  Multiplexer #(.select(3), .enable("false")) multiplexer_3 (
    .in1(adder_re_im_1_cout_re), .in2(sub_re_im_1_cout_re), .in3(mult_re_im_1_real_ov),
    .in4(div_re_im_1_real_ov), .out(COUT_RE), .sel(OPERATION));  // open: in0, in5, in6, in7
  Multiplexer #(.select(3), .enable("false")) multiplexer_4 (
    .in1(adder_re_im_1_cout_im), .in2(sub_re_im_1_cout_im), .in3(mult_re_im_1_imag_ov),
    .in4(div_re_im_1_imag_ov), .out(COUT_IM), .sel(OPERATION));  // open: in0, in5, in6, in7
  Multiplexer #(.select(3), .enable("false")) multiplexer_5 (
    .in0(1'b0), .in1(1'b0), .in2(1'b0), .in3(1'b0), .in4(div_re_im_1_div_0_error), .in5(1'b0), .in6(1'b0),
    .in7(1'b0), .out(DIV_BY_0), .sel(OPERATION));

  // Other names for the same wires on the sheet: cin_im_t = CIN_IM; cin_re_t = CIN_RE; im1_t[7:0] = B; im2_t[7:0] = D;
  //   re1_t[7:0] = A; re2_t[7:0] = C

  // Notes on the sheet:
  //   pierwsza liczba
  //   A-re, B-im
  //   C-re, D-im
  //   druga liczba
  //   wybór operacji
  //   001- dodawanie
  //   010 - odejmowanie
  //   011- mnozenie
  //   100- dzielenie
endmodule
