// Logisim project cos1.circ as structural Verilog: 1 circuit, main circuit main
module main (
  input  in_1,
  input  in_2,
  input  in_3,
  input  [7:0] in_4,
  input  in_5
);

  wire CLOCK_out;
  wire [7:0] instruction_adres_register_q, ram_1_data, register_1_q, register_5_q, register_6_q, register_7_q;

  Register register_1 (.D(ram_1_data), .Q(register_1_q));  // open: en, clk, clr
  Register #(.width(1)) register_2 ();  // open: D, en, Q, clk, clr
  Register #(.width(1)) register_3 ();  // open: D, en, Q, clk, clr
  Register #(.width(1)) register_4 ();  // open: D, en, Q, clk, clr
  Register register_5 (.D(ram_1_data), .Q(register_5_q));  // open: en, clk, clr
  Register register_6 (.D(ram_1_data), .Q(register_6_q));  // open: en, clk, clr
  Register register_7 (.D(ram_1_data), .Q(register_7_q));  // open: en, clk, clr
  Clock CLOCK (.out(CLOCK_out));
  Register instruction_register (.D(ram_1_data), .en(in_3), .clk(CLOCK_out));  // open: Q, clr
  Register instruction_adres_register (
    .D(in_4), .en(in_5), .clk(CLOCK_out), .Q(instruction_adres_register_q));  // open: clr
  RAM ram_1 (.addr(instruction_adres_register_q), .we(in_1), .oe(in_2), .clk(CLOCK_out), .data(ram_1_data));

  // Notes on the sheet:
  //   flagi
endmodule
