// Logisim project dekoder_enabler.circ as structural Verilog: 4 circuits, main circuit main
module main (
  input  [7:0] in_1,
  output [7:0] out_2,
  output [7:0] out_3
);

  wire [7:0] undriven;

  ROM rom_1 (.addr(in_1), .data(out_3));
  Dekoder_alfa dekoder_alfa_1 (.in_1(undriven), .out_2(out_2));

  // Notes on the sheet:
  //   contents of rom_1 (hex, n*v repeats v):
  //   8d
endmodule

module Dekoder_alfa (
  input  [7:0] in_1,
  output [7:0] out_2
);

  wire not_1_out, not_2_out, not_3_out, not_4_out;

  not not_1 (not_1_out, in_1[7]);
  not not_2 (not_2_out, in_1[6]);
  not not_3 (not_3_out, in_1[5]);
  not not_4 (not_4_out, in_1[4]);
  and ins_0001 (out_2[4], not_1_out, not_2_out, not_3_out, in_1[4]);
  and ins_0010 (out_2[5], not_1_out, not_2_out, in_1[5], not_4_out);
  and ins_0011 (out_2[6], not_1_out, not_2_out, in_1[5], in_1[4]);
  and ins_0100 (out_2[7], not_1_out, in_1[6], not_3_out, not_4_out);

  assign out_2[3:0] = 4'b0000;

  // Notes on the sheet:
  //   Dekoder
endmodule

module ENABLER_alfa (
  input  [7:0] in_1,
  input  ENABLE_,
  output [7:0] out_3
);

  wire and_1_out, and_2_out, and_3_out, and_4_out, and_5_out, and_6_out, and_7_out, and_8_out;

  and and_1 (and_1_out, in_1[0], ENABLE_);
  and and_2 (and_2_out, in_1[1], ENABLE_);
  and and_3 (and_3_out, in_1[2], ENABLE_);
  and and_4 (and_4_out, in_1[3], ENABLE_);
  and and_5 (and_5_out, in_1[4], ENABLE_);
  and and_6 (and_6_out, in_1[5], ENABLE_);
  and and_7 (and_7_out, in_1[6], ENABLE_);
  and and_8 (and_8_out, in_1[7], ENABLE_);
  assign out_3[0] = ENABLE_ ? and_1_out : 1'bz;  // Controlled_Buffer controlled_buffer_1
  assign out_3[1] = ENABLE_ ? and_2_out : 1'bz;  // Controlled_Buffer controlled_buffer_2
  assign out_3[2] = ENABLE_ ? and_3_out : 1'bz;  // Controlled_Buffer controlled_buffer_3
  assign out_3[3] = ENABLE_ ? and_4_out : 1'bz;  // Controlled_Buffer controlled_buffer_4
  assign out_3[4] = ENABLE_ ? and_5_out : 1'bz;  // Controlled_Buffer controlled_buffer_5
  assign out_3[5] = ENABLE_ ? and_6_out : 1'bz;  // Controlled_Buffer controlled_buffer_6
  assign out_3[6] = ENABLE_ ? and_7_out : 1'bz;  // Controlled_Buffer controlled_buffer_7
  assign out_3[7] = ENABLE_ ? and_8_out : 1'bz;  // Controlled_Buffer controlled_buffer_8

  // Notes on the sheet:
  //   ENABLER
endmodule

module flogic_functions (
  input  [7:0] in_1,
  output [7:0] out_2
);

  ROM rom_1 (.addr(in_1), .data(out_2));

  // Notes on the sheet:
  //   contents of rom_1 (hex, n*v repeats v):
  //   8d
endmodule
