// Logisim project przykladRAMHA.circ as structural Verilog: 2 circuits, main circuit main
module main (
  input  [7:0] in_1,
  input  in_2,
  input  in_3,
  input  in_4,
  input  in_5,
  input  in_6,
  input  in_7,
  input  [7:0] in_8,
  output out_9,
  output out_10,
  output [7:0] out_11
);

  wire clock_1_out;

  HalfAdder My_Half_Adder (.x1(in_4), .y1(in_3), .C(out_9), .S(out_10));
  Clock clock_1 (.out(clock_1_out));
  RAM ram_1 (.addr(in_1), .we(in_5), .oe(in_6), .clk(clock_1_out), .data(out_11));
  ROM rom_1 ();  // open: addr, data
endmodule

module HalfAdder (
  input  x1,
  input  y1,
  output C,
  output S
);

  and and_1 (C, x1, y1);
  xor xor_1 (S, x1, y1);
endmodule
