// Logisim project wielkanoc.circ as structural Verilog: 6 circuits, main circuit main
module main (
  input  in_1,
  input  in_2,
  input  in_3,
  input  [7:0] in_4,
  input  in_5,
  input  in_6
);

  wire CLK, clock_2_out, MAIN_ALU_carry_out, steps_clock_1_p2, steps_clock_1_p3, steps_clock_1_p4,
       steps_clock_1_p5, undriven, undriven_2, undriven_3, undriven_4, undriven_6, undriven_7, undriven_8,
       undriven_9, undriven_10, undriven_11;
  wire [7:0] bus_1_wtf_1_out, MAIN_ALU_out_from_alu, registerdeluxe_1_register_output, tmp_register_1_out_3,
       undriven_5;

  TMP_register tmp_register_1 (.in_1(registerdeluxe_1_register_output), .in_2(undriven), .out_3(tmp_register_1_out_3));
  registerDeluxe registerdeluxe_1 (
    .register_input(registerdeluxe_1_register_output), .register_output(registerdeluxe_1_register_output),
    .SET(in_1), .enable(in_3));  // open: reset
  ENABLER_alfa enabler_alfa_1 (.in_1(in_4), .ENABLE_(in_5), .out_3(registerdeluxe_1_register_output));
  bus_1_wtf bus_1_wtf_1 (.in(tmp_register_1_out_3), .bus_1wt(undriven_3), .out(bus_1_wtf_1_out));
  alu_alfa1 MAIN_ALU (
    .arg_A(registerdeluxe_1_register_output), .arg_B(bus_1_wtf_1_out), .carry_in(undriven_2),
    .cpu_inst(undriven_5), .carry_out(MAIN_ALU_carry_out), .out_from_alu(MAIN_ALU_out_from_alu));
  registerDeluxe registerdeluxe_2 (
    .register_input(registerdeluxe_1_register_output), .register_output(registerdeluxe_1_register_output));  // open: reset, SET, enable
  Clock clock_1 (.out(CLK));
  Clock clock_2 (.out(clock_2_out));
  registerDeluxe ACC (
    .register_input(MAIN_ALU_out_from_alu), .reset(undriven_6),
    .register_output(registerdeluxe_1_register_output), .SET(undriven_7), .enable(undriven_4));
  registerDeluxe registerdeluxe_3 (
    .register_input(registerdeluxe_1_register_output), .register_output(registerdeluxe_1_register_output));  // open: reset, SET, enable
  // steps_clock steps_clock_1: pin names not known; wires that end beside it: clock_2_out, steps_clock_1_p2, steps_clock_1_p3, steps_clock_1_p4, steps_clock_1_p5, steps_clock_1_p4, steps_clock_1_p4, steps_clock_1_p4, steps_clock_1_p5, steps_clock_1_p2, steps_clock_1_p3
  registerDeluxe registerdeluxe_4 (
    .register_input(registerdeluxe_1_register_output), .register_output(registerdeluxe_1_register_output));  // open: reset, SET, enable
  registerDeluxe IAR (
    .register_input(registerdeluxe_1_register_output), .register_output(registerdeluxe_1_register_output),
    .SET(undriven_8), .enable(undriven_9));  // open: reset
  // RAM ram_1: pin names not known; wires that end beside it: registerdeluxe_1_register_output[2], registerdeluxe_1_register_output[1], registerdeluxe_1_register_output[0]
  alu_alfa1 alu_alfa1_1 ();  // open: arg_A, arg_B, carry_in, cpu_inst, carry_out, out_from_alu
  registerDeluxe IR (
    .register_input(registerdeluxe_1_register_output), .register_output(registerdeluxe_1_register_output),
    .SET(undriven_10), .enable(undriven_11));  // open: reset

  // Notes on the sheet:
  //   76543210
  //   TMP reg
endmodule

module alu_alfa1 (
  input  [7:0] arg_A,
  input  [7:0] arg_B,
  input  carry_in,
  input  [7:0] cpu_inst,
  output carry_out,
  output [7:0] out_from_alu
);

  wire adder_1_cout, and_1_out, and_2_out, subtractor_1_bout;
  wire [7:0] adder_1_out, dekoder_alfa_1_out_2, divider_1_out, multiplier_1_out, subtractor_1_out;

  Adder adder_1 (.a(arg_A), .b(arg_B), .out(adder_1_out), .cin(carry_in), .cout(adder_1_cout));
  Subtractor subtractor_1 (.a(arg_A), .b(arg_B), .out(subtractor_1_out), .bin(carry_in), .bout(subtractor_1_bout));
  Multiplier multiplier_1 (.a(arg_A), .b(arg_B), .out(multiplier_1_out));  // open: cin, cout
  Divider divider_1 (.a(arg_A), .b(arg_B), .out(divider_1_out));  // open: upper, rem
  Dekoder_alfa dekoder_alfa_1 (.in_1(cpu_inst), .out_2(dekoder_alfa_1_out_2));
  ENABLER_alfa enabler_alfa_1 (.in_1(adder_1_out), .ENABLE_(dekoder_alfa_1_out_2[4]), .out_3(out_from_alu));
  ENABLER_alfa enabler_alfa_2 (.in_1(subtractor_1_out), .ENABLE_(dekoder_alfa_1_out_2[5]), .out_3(out_from_alu));
  ENABLER_alfa enabler_alfa_3 (.in_1(multiplier_1_out), .ENABLE_(dekoder_alfa_1_out_2[6]), .out_3(out_from_alu));
  ENABLER_alfa enabler_alfa_4 (.in_1(divider_1_out), .ENABLE_(dekoder_alfa_1_out_2[7]), .out_3(out_from_alu));
  and and_1 (and_1_out, adder_1_cout, dekoder_alfa_1_out_2[4]);
  assign carry_out = dekoder_alfa_1_out_2[4] ? and_1_out : 1'bz;  // Controlled_Buffer controlled_buffer_1
  and and_2 (and_2_out, dekoder_alfa_1_out_2[5], subtractor_1_bout);
  assign carry_out = dekoder_alfa_1_out_2[5] ? and_2_out : 1'bz;  // Controlled_Buffer controlled_buffer_2

  // Notes on the sheet:
  //   argument a
  //   argument b
  //   w operacjach dodac support dla zespolonych
  //   operacje
  //   istotne najwyzsze 4 bity tylko
  //   carry out
endmodule

module registerDeluxe (
  input  [7:0] register_input,
  input  SET,
  input  reset,
  input  enable,
  output [7:0] register_output
);

  wire CLK;
  wire [7:0] register_1_q;

  Register register_1 (.D(register_input), .en(SET), .clk(CLK), .Q(register_1_q), .clr(reset));
  ENABLER_alfa enabler_alfa_1 (.in_1(register_1_q), .ENABLE_(enable), .out_3(register_output));
endmodule

module TMP_register (
  input  [7:0] in_1,
  input  in_2,
  output [7:0] out_3
);

  wire CLK;
  wire [7:0] controlled_buffer_1_out;

  assign controlled_buffer_1_out = in_2 ? in_1 : 8'bz;  // Controlled_Buffer controlled_buffer_1
  Register register_1 (.D(controlled_buffer_1_out), .en(in_2), .clk(CLK), .Q(out_3));  // open: clr
endmodule

module bus_1_wtf (
  input  [7:0] in,
  input  bus_1wt,
  output [7:0] out
);

  wire not_1_out;

  and and_1 (out[7], not_1_out, in[7]);
  and and_2 (out[6], not_1_out, in[6]);
  and and_3 (out[5], not_1_out, in[5]);
  and and_4 (out[4], not_1_out, in[4]);
  and and_5 (out[3], not_1_out, in[3]);
  and and_6 (out[1], not_1_out, in[1]);
  and and_7 (out[2], not_1_out, in[2]);
  not not_1 (not_1_out, bus_1wt);
  or or_1 (out[0], in[0], bus_1wt);
endmodule

module steps_clock (
  input  reset,
  input  clock,
  output step_3,
  output step_4,
  output step_6,
  output step_7,
  output step_1,
  output step_2,
  output step_5
);

  wire d_ff_1_q, d_ff_2_q, d_ff_3_q, d_ff_4_q, d_ff_5_q, d_ff_6_q, d_ff_7_q, d_ff_8_q, d_ff_9_q, d_ff_10_q,
       d_ff_11_q, d_ff_12_q, d_ff_13_q, d_ff_14_q, not_1_out, not_2_out, not_4_out, not_5_out, not_6_out,
       not_7_out, not_8_out, not_9_out, or_1_out, or_2_out, or_3_out;

  not not_1 (not_1_out, clock);
  not not_2 (not_2_out, reset);
  or or_1 (or_1_out, 1'b0, clock);
  or or_2 (or_2_out, 1'b0, not_1_out);
  D_Flip_Flop d_ff_1 (.D(not_2_out), .clk(or_1_out), .Q(d_ff_1_q), .reset(or_3_out));  // open: Qn, preset
  D_Flip_Flop d_ff_2 (.D(d_ff_1_q), .clk(or_2_out), .Q(d_ff_2_q), .reset(or_3_out));  // open: Qn, preset
  not not_3 (step_1, d_ff_2_q);
  and and_1 (step_2, d_ff_2_q, not_4_out);
  D_Flip_Flop d_ff_3 (.D(d_ff_2_q), .clk(or_1_out), .Q(d_ff_3_q), .reset(or_3_out));  // open: Qn, preset
  not not_4 (not_4_out, d_ff_4_q);
  D_Flip_Flop d_ff_4 (.D(d_ff_3_q), .clk(or_2_out), .Q(d_ff_4_q), .reset(or_3_out));  // open: Qn, preset
  and and_2 (step_3, d_ff_4_q, not_5_out);
  D_Flip_Flop d_ff_5 (.D(d_ff_4_q), .clk(or_1_out), .Q(d_ff_5_q), .reset(or_3_out));  // open: Qn, preset
  not not_5 (not_5_out, d_ff_6_q);
  D_Flip_Flop d_ff_6 (.D(d_ff_5_q), .clk(or_2_out), .Q(d_ff_6_q), .reset(or_3_out));  // open: Qn, preset
  and and_3 (step_4, d_ff_6_q, not_6_out);
  D_Flip_Flop d_ff_7 (.D(d_ff_6_q), .clk(or_1_out), .Q(d_ff_7_q), .reset(or_3_out));  // open: Qn, preset
  not not_6 (not_6_out, d_ff_8_q);
  D_Flip_Flop d_ff_8 (.D(d_ff_7_q), .clk(or_2_out), .Q(d_ff_8_q), .reset(or_3_out));  // open: Qn, preset
  and and_4 (step_5, d_ff_8_q, not_7_out);
  D_Flip_Flop d_ff_9 (.D(d_ff_8_q), .clk(or_1_out), .Q(d_ff_9_q), .reset(or_3_out));  // open: Qn, preset
  not not_7 (not_7_out, d_ff_10_q);
  D_Flip_Flop d_ff_10 (.D(d_ff_9_q), .clk(or_2_out), .Q(d_ff_10_q), .reset(or_3_out));  // open: Qn, preset
  and and_5 (step_6, d_ff_10_q, not_8_out);
  D_Flip_Flop d_ff_11 (.D(d_ff_10_q), .clk(or_1_out), .Q(d_ff_11_q), .reset(or_3_out));  // open: Qn, preset
  not not_8 (not_8_out, d_ff_12_q);
  D_Flip_Flop d_ff_12 (.D(d_ff_11_q), .clk(or_2_out), .Q(d_ff_12_q), .reset(or_3_out));  // open: Qn, preset
  and and_6 (step_7, d_ff_12_q, not_9_out);
  D_Flip_Flop d_ff_13 (.D(d_ff_12_q), .clk(or_1_out), .Q(d_ff_13_q), .reset(or_3_out));  // open: Qn, preset
  not not_9 (not_9_out, d_ff_14_q);
  D_Flip_Flop d_ff_14 (.D(d_ff_13_q), .clk(or_2_out), .Q(d_ff_14_q), .reset(or_3_out));  // open: Qn, preset
  or or_3 (or_3_out, reset, d_ff_14_q);
endmodule
